# Fritzing sketch receiver_schematic (saved by Fritzing 0.9.3b)

parts:
  Mod1 = Raspberry Pi Pico
  Part1 = NRF24L01+ Breakout Board
  Part2 = Bluetooth HC-05 Macho
  M1 = DC Motor
  S1 = H-Bridge with L298N
  S2 = H-Bridge with L298N
  M3 = DC Motor
  M5 = DC Motor
  M6 = DC Motor
  D3 = Rectifier Diode [part_number=1N4001 package="300 mil [THT]"]
  D4 = Rectifier Diode [part_number=1N4001 package="300 mil [THT]"]
  D1 = Rectifier Diode [part_number=1N4001 package="300 mil [THT]"]
  D2 = Rectifier Diode [part_number=1N4001 package="300 mil [THT]"]
  VCC1 = 4 x AAA Battery Mount

nets:
  N1: Mod1.pin_1, S2.IN1
  N2: Mod1.pin_2, Mod1.pin_3, Mod1.pin_38, Mod1.pin_42, Part1.GND, S2.IN2, D3.anode, D1.anode
  N3: Mod1.pin_4, S2.IN3
  N4: Mod1.pin_5, S2.IN4
  N5: Mod1.pin_6, Part1.MISO
  N6: Mod1.pin_9, Part1.SCK
  N7: Mod1.pin_10, Part1.MOSI
  N8: Mod1.pin_17, Part2.TXD
  N9: Mod1.pin_19, Part1.CE
  N10: Mod1.pin_20, Part1.CS
  N11: Mod1.pin_25, S1.IN3
  N12: Mod1.pin_26, S1.IN2
  N13: Mod1.pin_27, S1.IN1
  N14: Mod1.pin_36, Mod1.pin_37, Part1.VCC
  N15: Mod1.pin_39, D4.cathode, D2.cathode
  N16: M1.pin_1, S2.M2-02
  N17: M1.pin_2, S2.M2-01
  12V: S1.12V, S2.12V, VCC1.+
  GND: S1.GND, S2.GND, D1.cathode, VCC1.-
  N18: S1.ENA, S1.ENA-5V
  N19: S1.ENB, S1.ENB-5V
  N20: S1.M1-01, M6.pin_2
  N21: S1.M1-02, M6.pin_1
  N22: S1.M2-01, M3.pin_2
  N23: S1.M2-02, M3.pin_1
  N24: S2.5V, D2.anode
  N25: S2.M1-02, M5.pin_1

custom parts:
  Raspberry Pi Pico: Raspberry Pi Pico. Based around the RP2040 microcontroller the Pico is a low cost microcontroller device bringing Raspberry Pi quality, cost, and easy of use to the microcontroller space. Jan 2021, Split part in to two versions: tht (this one) and SMD. This one will drill holes for a .1 in header in pcb to allow plugging in the module as well as providing pads to solder the module to the top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
  H-Bridge with L298N: h-bridge
