# Fritzing sketch transmitter_schematic (saved by Fritzing 0.9.3b)

parts:
  Mod1 = Raspberry Pi Pico
  Part1 = NRF24L01+ Breakout Board
  Part2 = Thumb Joystick
  Part3 = Thumb Joystick
  Grove1 = Grove OLED 128x96

nets:
  GND: Mod1.pin_2, Mod1.pin_3, Mod1.pin_23, Mod1.pin_33, Mod1.pin_42, Part1.GND, Part2.GND, Grove1.GND
  N1: Mod1.pin_6, Part1.MISO
  N2: Mod1.pin_9, Part1.SCK
  N3: Mod1.pin_10, Part1.MOSI
  N4: Mod1.pin_19, Part1.CE
  N5: Mod1.pin_20, Part1.CS
  N6: Mod1.pin_21, Grove1.SDA
  N7: Mod1.pin_22, Grove1.SCL
  N8: Mod1.pin_31, Part2.HORZ
  N9: Mod1.pin_32, Part2.VERT
  N10: Mod1.pin_34, Part3.VERT
  N11: Mod1.pin_36, Mod1.pin_37, Part1.VCC

custom parts:
  Raspberry Pi Pico: Raspberry Pi Pico. Based around the RP2040 microcontroller the Pico is a low cost microcontroller device bringing Raspberry Pi quality, cost, and easy of use to the microcontroller space. Jan 2021, Split part in to two versions: tht (this one) and SMD. This one will drill holes for a .1 in header in pcb to allow plugging in the module as well as providing pads to solder the module to the top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
